# Fritzing sketch sadetin (saved by Fritzing 0.9.3b)
breadboards: 1

parts:
  Part1 = Arduino Uno (Rev3)
  LCD1 = LCD screen  # not connected
  U3 = BME-BMP-280 [chip_label=BME/BMP280 package=THT]
  R1 = Resistor [tolerance=±5% resistance=10k package="0805 [SMD]"]
  S1 = Pushbutton [package=THT]
  S2 = Pushbutton [package=THT]
  R2 = Resistor [tolerance=±5% resistance=10k package="0805 [SMD]"]

nets:
  N1: Part1.A4/SDA, U3.VIN
  N2: Part1.A5/SCL, U3.GND
  N3: Part1.D8, R1.Pin_0, S1.leg0
  N4: Part1.D7, S2.leg1, R2.Pin_1
  N5: Part1.5V, U3.SDA, S1.leg1, S2.leg0
  N6: Part1.GND, U3.SCL, R1.Pin_1, R2.Pin_0

custom parts:
  BME-BMP-280: Bosch oikea
